# Fritzing sketch Wireless Temperature Data Logger (saved by Fritzing 0.9.0b)
breadboards: 2

parts:
  LCD1 = LCD screen
  R1 = Trimmer Potentiometer [maximum_resistance=10kΩ package=THT]
  S1 = Pushbutton [package="[THT]"]
  S2 = Pushbutton [package="[THT]"]
  S3 = Pushbutton [package="[THT]"]
  S4 = Pushbutton [package="[THT]"]
  S5 = Pushbutton [package="[THT]"]
  S6 = Pushbutton [package="[THT]"]
  R2 = Resistor [tolerance=±5% resistance=220 package=THT]
  R3 = Resistor [tolerance=±5% resistance=220 package=THT]
  R4 = Resistor [tolerance=±5% resistance=220 package=THT]
  R5 = Resistor [tolerance=±5% resistance=220 package=THT]
  U4 = mystery part, 8 pins [chip_label="RF Receiver" spacing=300mil]
  U5 = mystery part, 8 pins [chip_label=MicroSD spacing=300mil]
  T1 = Temperature Sensor (Thermistor) [thermistor_type=NTC package=THT]
  LED1 = LED - 5mm [color="Green (555nm)" package="5 mm [THT]"]  # not connected
  R6 = Resistor [tolerance=±5% resistance=10k package=THT]
  VCC1 = Battery block 9V  # not connected
  VCC2 = Battery block 9V  # not connected
  U6 = mystery part, 4 pins [chip_label="RF Transmitter" spacing=300mil]
  R7 = Resistor [tolerance=±5% resistance=10k package=THT]
  T2 = Temperature Sensor (Thermistor) [thermistor_type=NTC package=THT]
  U1 = Arduino Mega 2560 (Rev3)
  Arduino1 = Arduino Uno (Rev3)

nets:
  VSS: LCD1.VSS, LCD1.R/W, LCD1.LED-, R1.leg2, S1.Pin_3, S1.Pin_4, S2.Pin_3, S2.Pin_4, S3.Pin_3, S3.Pin_4, S4.Pin_3, S4.Pin_4, S5.Pin_3, S5.Pin_4, S6.Pin_3, S6.Pin_4, R2.Pin_0, R2.Pin_1, R3.Pin_0, R3.Pin_1, R4.Pin_0, R4.Pin_1, R5.Pin_0, R5.Pin_1, U4.pin1, U4.pin6, U4.pin7, U5.pin3, R6.Pin_0, U1.A0, U1.GND
  N1: LCD1.V0, R1.wiper
  N2: U4.pin2, U1.D30
  N3: U4.pin4, U4.pin5, U5.pin1, T1.pin_1
  N4: U5.pin4, U1.D52
  N5: U5.pin5, U1.D50
  N6: U5.pin6, U1.D51
  N7: U5.pin7, U1.D53
  N8: T1.pin_0, R6.Pin_1, U1.A15
  N9: U6.pin3, T2.pin_1
  N10: R7.Pin_1, T2.pin_0, Arduino1.A0
